// Logisim project ALU.circ as structural Verilog
module AU (
  input  [7:0] A1,
  input  [7:0] A2,
  input  C1,
  output [7:0] out_4
);

  wire [7:0] adder_1_out, multiplexer_1_out, not_1_out;

  Adder adder_1 (.a(8'h1), .b(not_1_out), .out(adder_1_out));  // open: cin, cout
  assign not_1_out = ~A1;  // NOT_Gate not_1, 8 bits wide
  Multiplexer #(.enable("false"), .width(8)) multiplexer_1 (
    .in0(adder_1_out), .in1(A1), .out(multiplexer_1_out), .sel(C1));
  Adder adder_2 (.a(multiplexer_1_out), .b(A2), .out(out_4));  // open: cin, cout

  // Notes on the sheet:
  //   0-     1+
endmodule

module LU (
  input  [7:0] B1,
  input  [7:0] B2,
  input  C2,
  output [7:0] out_4
);

  wire [7:0] and_1_out, or_1_out;

  assign or_1_out = B1 | B2;  // OR_Gate or_1, 8 bits wide
  assign and_1_out = B1 & B2;  // AND_Gate and_1, 8 bits wide
  Multiplexer #(.enable("false"), .width(8)) multiplexer_1 (.in0(or_1_out), .in1(and_1_out), .out(out_4), .sel(C2));

  // Notes on the sheet:
  //   0 or 1 and
endmodule

module ALU (
  input  [7:0] in_1,
  input  [7:0] in_2,
  input  [3:0] in_3,
  output [7:0] out_4
);

  wire [7:0] au_1_out_4, lu_1_out_4;

  LU lu_1 (.B1(in_1), .B2(in_2), .C2(in_3[0]), .out_4(lu_1_out_4));
  AU au_1 (.A1(in_1), .A2(in_2), .C1(in_3[1]), .out_4(au_1_out_4));
  Multiplexer #(.enable("false"), .width(8)) multiplexer_1 (
    .in0(lu_1_out_4), .in1(au_1_out_4), .out(out_4), .sel(in_3[2]));

  // Notes on the sheet:
  //   x000 lu or
  //   x001 lu and
  //   x100 au -
  //   x110 au +
endmodule

module RegisterGroup (
  input  [4:0] in_1,
  input  [7:0] Data,
  input  [4:0] Address,
  input  WE,
  input  in_5,
  output [7:0] out_6
);

  wire and_1_out, and_2_out, and_3_out, and_4_out, and_5_out, and_6_out, and_7_out, and_8_out,
       decoder_1_out0, decoder_1_out1, decoder_1_out2, decoder_1_out3, decoder_1_out4, decoder_1_out5,
       decoder_1_out7;
  wire [7:0] register_1_q, register_2_q, register_3_q, register_4_q, register_5_q, register_6_q,
       register_7_q, register_8_q;

  Decoder #(.select(3)) decoder_1 (
    .out0(decoder_1_out0), .out1(decoder_1_out1), .out2(decoder_1_out2), .out3(decoder_1_out3),
    .out4(decoder_1_out4), .out5(decoder_1_out5), .out6(decoder_1_out5), .out7(decoder_1_out7));  // open: sel, en
  and and_1 (and_1_out, decoder_1_out0, WE);
  and and_2 (and_2_out, decoder_1_out1, WE);
  and and_3 (and_3_out, decoder_1_out2, WE);
  and and_4 (and_4_out, decoder_1_out3, WE);
  and and_5 (and_5_out, decoder_1_out4, WE);
  and and_6 (and_6_out, decoder_1_out5, WE);
  and and_7 (and_7_out, decoder_1_out5, WE);
  and and_8 (and_8_out, decoder_1_out7, WE);
  Register register_1 (.D(Data), .en(and_1_out), .clk(in_5), .Q(register_1_q));  // open: clr
  Register register_2 (.D(Data), .en(and_2_out), .clk(in_5), .Q(register_2_q));  // open: clr
  Register register_3 (.D(Data), .en(and_3_out), .clk(in_5), .Q(register_3_q));  // open: clr
  Register register_4 (.D(Data), .en(and_4_out), .clk(in_5), .Q(register_4_q));  // open: clr
  Register register_5 (.D(Data), .en(and_5_out), .clk(in_5), .Q(register_5_q));  // open: clr
  Register register_6 (.D(Data), .en(and_6_out), .clk(in_5), .Q(register_6_q));  // open: clr
  Register register_7 (.D(Data), .en(and_7_out), .clk(in_5), .Q(register_7_q));  // open: clr
  Register register_8 (.D(Data), .en(and_8_out), .clk(in_5), .Q(register_8_q));  // open: clr
  Multiplexer #(.enable("false"), .select(3), .width(8)) multiplexer_1 (
    .in0(register_1_q), .in1(register_2_q), .in2(register_3_q), .in3(register_4_q), .in4(register_5_q),
    .in5(register_6_q), .in6(register_7_q), .in7(register_8_q), .out(out_6), .sel(in_1[2:0]));
endmodule
